# Fritzing sketch potato_drum (saved by Fritzing 0.9.2b)
breadboards: 1

parts:
  Raspberry_Pi1 = Raspberry Pi 2
  Part3 = MPR121 Breakout

nets:
  3V3: Raspberry_Pi1.3v3, Part3.3.3V
  N1: Raspberry_Pi1.GPIO2, Part3.SDA
  N2: Raspberry_Pi1.GPIO3, Part3.SCL
  N3: Raspberry_Pi1.GPIO14, Part3.~IRQ
  GND: Raspberry_Pi1.GND, Part3.GND
